# Fritzing sketch scheme (saved by Fritzing 0.9.3b)
breadboards: 1

parts:
  Part2 = Arduino Nano (Rev3.0)
  S1 = Momentary Switch [package=ksa_sealed_tac_switch]
  S2 = Momentary Switch [package=ksa_sealed_tac_switch]
  KY-1 = Keyes Relay [package=THT]
  KY-2 = Keyes Relay [package=THT]
  KY-3 = Keyes Relay [package=THT]
  KY-4 = Keyes Relay [package=THT]
  DFRobot_DFPlayer_Mini2 = DFRobot DFPlayer Mini [part_number=DFR0299]
  SP2 = SPEAKER [package=pcb_mount_speaker]
  R3 = Resistor [tolerance=±5% resistance=1k package="0805 [SMD]"]
  R4 = Resistor [tolerance=±5% resistance=1k package="0805 [SMD]"]
  S3 = Momentary Switch [package=ksa_sealed_tac_switch]
  S4 = Momentary Switch [package=ksa_sealed_tac_switch]

nets:
  N1: Part2.GND, S1.2, S2.2, KY-1.ground, DFRobot_DFPlayer_Mini2.GND-1, DFRobot_DFPlayer_Mini2.GND-2, S3.2, S4.2
  N2: Part2.D2, S4.4
  N3: Part2.D3, S3.4
  N4: Part2.D4, S2.4
  N5: Part2.D5, S1.4
  N6: Part2.D6, KY-3.signal
  N7: Part2.D7, KY-1.signal
  N8: Part2.D8, KY-2.ground
  N9: Part2.D9, KY-4.signal
  N10: Part2.D10, R4.Pin_0
  N11: Part2.D11/MOSI, R3.Pin_0
  5V: Part2.5V, KY-1.power, DFRobot_DFPlayer_Mini2.VCC
  N12: DFRobot_DFPlayer_Mini2.RX, R3.Pin_1
  N13: DFRobot_DFPlayer_Mini2.TX, R4.Pin_1
  N14: DFRobot_DFPlayer_Mini2.SPK_1, SP2.-
  N15: DFRobot_DFPlayer_Mini2.SPK_2, SP2.+

notes:
  4 Relay Sensor - NANO
  VCC - 5V
  GND - GND
  SIG1 - D6
  SIG2 - D7
  SIG3 - D8
  SIG4 - D9
  Button - NANO
  GND - GND
  SIG1 - D2
  SIG2 - D3
  SIG3 - D4
  SIG4 - D5
  1 кОм

custom parts:
  Keyes Relay: The Keyes 5V relay module is suitable for SCM development, home appliance control. It uses a 5V~12V TIL control signal which can control DC / AC signal.
